// Logisim project 6551071088_LAB2_Bài3.circ as structural Verilog: 1 circuit, main circuit main
module main (
  input  [3:0] A,
  input  [3:0] B
);

  wire and_1_out, and_2_out, and_3_out, and_4_out, and_5_out, and_6_out, and_7_out, and_8_out, or_1_out,
       or_2_out, or_4_out, xor_1_out, xor_2_out, xor_3_out, xor_4_out;

  xor xor_1 (xor_1_out, A[0], B[0]);
  xor xor_2 (xor_2_out, A[1], B[1]);
  xor xor_3 (xor_3_out, A[2], B[2]);
  xor xor_4 (xor_4_out, A[3], B[3]);
  // XOR_Gate xor_5 has open pins: in0=xor_1_out, in1=1'b0, out=open
  and and_1 (and_1_out, A[0], B[0]);
  and and_2 (and_2_out, xor_1_out, 1'b0);
  // XOR_Gate xor_6 has open pins: in0=xor_2_out, in1=or_4_out, out=open
  and and_3 (and_3_out, A[1], B[1]);
  and and_4 (and_4_out, xor_2_out, or_4_out);
  // XOR_Gate xor_7 has open pins: in0=xor_3_out, in1=or_1_out, out=open
  and and_5 (and_5_out, A[2], B[2]);
  and and_6 (and_6_out, xor_3_out, or_1_out);
  // XOR_Gate xor_8 has open pins: in0=xor_4_out, in1=or_2_out, out=open
  and and_7 (and_7_out, A[3], B[3]);
  and and_8 (and_8_out, xor_4_out, or_2_out);
  or or_1 (or_1_out, and_3_out, and_4_out);
  or or_2 (or_2_out, and_5_out, and_6_out);
  // OR_Gate or_3 has open pins: in0=and_7_out, in1=and_8_out, out=open
  or or_4 (or_4_out, and_1_out, and_2_out);

  // Notes on the sheet:
  //   Huỳnh Nguyễn Minh Triển _ 6551071088
endmodule
