// Logisim project 6551071088_LAB2_Bài4.circ as structural Verilog: 1 circuit, main circuit main
module main (
  input  [3:0] A,
  input  [3:0] B,
  output [3:0] Diff,
  output Borrow
);

  wire and_1_out, and_2_out, and_3_out, and_4_out, and_5_out, and_6_out, and_7_out, and_8_out, not_1_out,
       not_2_out, not_3_out, not_4_out, or_1_out, or_2_out, or_3_out, or_4_out, xor_1_out, xor_2_out,
       xor_3_out, xor_4_out;

  not not_1 (not_1_out, B[0]);
  not not_2 (not_2_out, B[1]);
  not not_3 (not_3_out, B[2]);
  not not_4 (not_4_out, B[3]);
  xor xor_1 (xor_1_out, A[0], not_1_out);
  xor xor_2 (xor_2_out, A[1], not_2_out);
  xor xor_3 (xor_3_out, A[2], not_3_out);
  xor xor_4 (xor_4_out, A[3], not_4_out);
  xor xor_5 (Diff[0], xor_1_out, 1'b1);
  and and_1 (and_1_out, A[0], not_1_out);
  and and_2 (and_2_out, xor_1_out, 1'b1);
  xor xor_6 (Diff[1], xor_2_out, or_3_out);
  and and_3 (and_3_out, A[1], not_2_out);
  and and_4 (and_4_out, xor_2_out, or_3_out);
  xor xor_7 (Diff[2], xor_3_out, or_1_out);
  and and_5 (and_5_out, A[2], not_3_out);
  and and_6 (and_6_out, xor_3_out, or_1_out);
  xor xor_8 (Diff[3], xor_4_out, or_2_out);
  and and_7 (and_7_out, A[3], not_4_out);
  and and_8 (and_8_out, xor_4_out, or_2_out);
  or or_1 (or_1_out, and_3_out, and_4_out);
  or or_2 (or_2_out, and_5_out, and_6_out);
  or or_3 (or_3_out, and_1_out, and_2_out);
  or or_4 (or_4_out, and_7_out, and_8_out);
  not not_5 (Borrow, or_4_out);
endmodule
