// Logisim project 6551071088_LAB2_Bài5.circ as structural Verilog: 1 circuit, main circuit main
module main (
  input  [3:0] A,
  input  [3:0] B,
  output A_B,
  output A_B_2,
  output A_B_3
);

  Comparator #(.width(4)) comparator_1 (.a(A), .b(B), .gt(A_B), .eq(A_B_2), .lt(A_B_3));

  // Notes on the sheet:
  //   Huỳnh Nguyễn Minh Triển _ 6551071088
endmodule
