// Logisim project 6551071088_LAB2_Bài6.circ as structural Verilog: 1 circuit, main circuit main
module main (
  input  EN,
  input  Resert,
  output [3:0] out_3
);

  wire clock_1_out, j_k_ff_1_qn, j_k_ff_2_qn, j_k_ff_3_qn;

  Clock clock_1 (.out(clock_1_out));
  J_K_Flip_Flop j_k_ff_1 (
    .J(EN), .clk(clock_1_out), .K(EN), .Q(out_3[0]), .Qn(j_k_ff_1_qn), .reset(Resert));  // open: preset, en
  J_K_Flip_Flop j_k_ff_2 (
    .J(EN), .clk(j_k_ff_1_qn), .K(EN), .Q(out_3[1]), .Qn(j_k_ff_2_qn), .reset(Resert));  // open: preset, en
  J_K_Flip_Flop j_k_ff_3 (
    .J(EN), .clk(j_k_ff_2_qn), .K(EN), .Q(out_3[2]), .Qn(j_k_ff_3_qn), .reset(Resert));  // open: preset, en
  J_K_Flip_Flop j_k_ff_4 (.J(EN), .clk(j_k_ff_3_qn), .K(EN), .Q(out_3[3]), .reset(Resert));  // open: Qn, preset, en

  // Notes on the sheet:
  //   Huỳnh Nguyễn Minh Triển _ 6551071088 
endmodule
