// Logisim project 6551071088_LAB2_Bài7.circ as structural Verilog: 1 circuit, main circuit main
module main (
  input  [2:0] Addr,
  input  [3:0] DataIn,
  input  Load,
  output [3:0] DataOut
);

  wire clock_1_out;

  Clock clock_1 (.out(clock_1_out));
  RAM #(.addrWidth(3), .dataWidth(4), .bus("separate")) ram_1 (
    .addr(Addr), .din(DataIn), .data(DataOut), .str(Load), .sel(1'b1), .clk(clock_1_out), .ld(1'b1),
    .clr(1'b0));

  // Notes on the sheet:
  //   Huỳnh Nguyễn Minh Triển _ 6551071088
endmodule
